// Logisim project F3.circ as structural Verilog: 21 circuits, main circuit main
module main (
  input  \或门 ,
  input  in_2,
  input  \异或门 ,
  input  in_4,
  input  \同或门 ,
  input  in_6,
  input  \_2_4译码器 ,
  input  in_8,
  input  in_9,
  input  in_10,
  input  in_11,
  input  in_12,
  input  in_13,
  input  in_14,
  input  in_15,
  input  in_16,
  input  in_17,
  input  in_18,
  input  in_19,
  input  in_20,
  input  in_21,
  input  in_22,
  input  in_23,
  input  in_24,
  input  in_25,
  input  in_26,
  input  in_27,
  input  in_28,
  input  in_29,
  input  in_30,
  input  in_31,
  input  in_32,
  input  in_33,
  input  A0,
  input  A1,
  input  A2,
  input  A3,
  input  in_38,
  input  in_39,
  input  in_40,
  input  in_41,
  input  in_42,
  input  in_43,
  input  in_44,
  input  in_45,
  input  in_46,
  input  in_47,
  input  num0,
  input  num1,
  input  num2,
  input  num3,
  input  point,
  input  switch,
  input  in_54,
  input  in_55,
  input  in_56,
  input  in_57,
  input  in_58,
  input  in_59,
  input  in_60,
  input  in_61,
  input  A,
  input  B,
  input  in_64,
  input  in_65,
  input  in_66,
  input  in_67,
  input  in_68,
  input  in_69,
  input  in_70,
  input  in_71,
  input  in_72,
  input  in_73,
  input  in_74,
  input  in_75,
  input  in_76,
  input  in_77,
  input  in_78,
  input  in_79,
  input  in_80,
  input  in_81,
  input  in_82,
  input  in_83,
  input  in_84,
  input  in_85,
  input  in_86,
  input  in_87,
  input  in_88,
  output out_89,
  output out_90,
  output out_91,
  output out_92,
  output out_93,
  output out_94,
  output out_95,
  output out_96,
  output Y0,
  output Y1,
  output out_99,
  output out_100,
  output out_101,
  output S,
  output C,
  output out_104,
  output out_105,
  output out_106,
  output out_107,
  output out_108,
  output out_109,
  output out_110,
  output out_111,
  output out_112,
  output out_113
);

  wire add4bit_1_c, add4bit_1_s0, add4bit_1_s1, add4bit_1_s2, add4bit_1_s3, add_1_cout, add_2_cout,
       add_3_cout, and_1_out, and_2_out, and_3_out, and_4_out, and_5_out, and_6_out, and_7_out, and_8_out,
       and_9_out, and_10_out, and_11_out, and_13_out, and_14_out, and_21_out, and_22_out, and_26_out,
       and_27_out, bit1select2_1_out0, bit1select2_2_out0, bit1select2_3_out0, bit1select2_4_out0,
       bit1select2_5_out0, bit1select2_6_out0, bit1select2_7_out0, bit1select2_8_out0,
       bit1select2for4bit_1_out0, bit1select2for4bit_1_out1, bit1select2for4bit_1_out2,
       bit1select2for4bit_1_out3, decoder2to4_1_out1, decoder2to4_1_out2, decoder2to4_1_out3,
       decoder2to4_1_out4, decoder2to4_2_out1, decoder2to4_2_out2, decoder2to4_2_out3, decoder2to4_2_out4,
       encoder16to4_1_out0, encoder16to4_1_out1, encoder16to4_1_out2, encoder16to4_1_out3, nor_1_out,
       nor_2_out, nor_3_out, not_1_out, not_2_out, not_3_out, not_4_out, not_5_out, not_6_out, not_7_out,
       not_8_out, not_9_out, number7decoder_1_a, number7decoder_1_b, number7decoder_1_c, number7decoder_1_d,
       number7decoder_1_e, number7decoder_1_f, number7decoder_1_g, number7decoder_1_h, number7decoder_2_a,
       number7decoder_2_b, number7decoder_2_c, number7decoder_2_d, number7decoder_2_e, number7decoder_2_f,
       number7decoder_2_g, number7decoder_2_h, number7decoder_3_a, number7decoder_3_b, number7decoder_3_c,
       number7decoder_3_d, number7decoder_3_e, number7decoder_3_f, number7decoder_3_g, number7decoder_3_h,
       number7decoder_4_a, number7decoder_4_b, number7decoder_4_c, number7decoder_4_d, number7decoder_4_e,
       number7decoder_4_f, number7decoder_4_g, number7decoder_5_a, number7decoder_5_b, number7decoder_5_c,
       number7decoder_5_d, number7decoder_5_e, number7decoder_5_f, number7decoder_5_g, number7decoder_5_h,
       number7decoder_6_a, number7decoder_6_b, number7decoder_6_c, number7decoder_6_d, number7decoder_6_e,
       number7decoder_6_f, number7decoder_6_g, number7decoder_6_h, number7decoder_7_a, number7decoder_7_b,
       number7decoder_7_c, number7decoder_7_d, number7decoder_7_e, number7decoder_7_f, number7decoder_7_g,
       number7decoder_7_h, number7decoder_8_a, number7decoder_8_b, number7decoder_8_c, number7decoder_8_d,
       number7decoder_8_e, number7decoder_8_f, number7decoder_8_g, number7decoder_9_a, number7decoder_9_b,
       number7decoder_9_c, number7decoder_9_d, number7decoder_9_e, number7decoder_9_f, number7decoder_9_g,
       number7decoderdex_1_b, number7decoderdex_1_c, number7decoderdex_1_d, number7decoderdex_1_e,
       number7decoderdex_1_f, number7decoderdex_1_g, number7decoderdex_1_h, or_1_out, or_5_out, or_6_out,
       sub4bitorigin_1_s0, sub4bitorigin_1_s1, sub4bitorigin_1_s2, sub4bitorigin_1_s3, sub4bitorigin_1_sign,
       sub_1_cout, sub_2_cout, sub_3_cout, transistor_1_out, transistor_2_out, transistor_5_out, xnor_1_out,
       xnor_2_out, xnor_3_out, xnor_4_out;

  not not_1 (not_1_out, \_2_4译码器 );
  Transistor #(.\type ("n")) transistor_1 (.in(1'b0), .out(transistor_1_out), .gate(\或门 ));
  and and_1 (and_1_out, \异或门 , in_4);
  and and_2 (and_2_out, \同或门 , in_6);
  not not_2 (not_2_out, in_8);
  and and_3 (and_3_out, \_2_4译码器 , in_8);
  // Probe on and_3_out
  not not_3 (not_3_out, in_11);
  Transistor transistor_2 (.in(1'b1), .out(transistor_2_out), .gate(\或门 ));
  Transistor transistor_3 (.in(transistor_2_out), .out(transistor_1_out), .gate(in_2));
  Transistor #(.\type ("n")) transistor_4 (.in(1'b0), .out(transistor_1_out), .gate(in_2));
  nor nor_1 (nor_1_out, \异或门 , in_4);
  nor nor_2 (nor_2_out, \同或门 , in_6);
  and and_4 (and_4_out, \_2_4译码器 , not_2_out);
  // Probe on and_4_out
  not not_4 (not_4_out, in_39);
  not not_5 (not_5_out, in_42);
  not not_6 (not_6_out, in_46);
  Transistor transistor_5 (.in(1'b1), .out(transistor_5_out), .gate(transistor_1_out));
  LED led_1 (.in(transistor_5_out));
  Transistor #(.\type ("n")) transistor_6 (.in(1'b0), .out(transistor_5_out), .gate(transistor_1_out));
  nor nor_3 (nor_3_out, and_1_out, nor_1_out);
  LED led_2 (.in(nor_3_out));
  or or_1 (or_1_out, and_2_out, nor_2_out);
  LED led_3 (.in(or_1_out));
  and and_5 (and_5_out, not_1_out, in_8);
  // Probe on and_5_out
  // Probe on and_13_out
  not not_7 (not_7_out, A2);
  and and_6 (and_6_out, in_38, not_4_out);
  and and_7 (and_7_out, in_39, in_40);
  and and_8 (and_8_out, in_41, not_5_out);
  and and_9 (and_9_out, in_42, in_43);
  and and_10 (and_10_out, in_45, not_6_out);
  and and_11 (and_11_out, in_46, in_47);
  xor xor_1 (S, A, B);
  and and_12 (C, A, B);
  and and_13 (and_13_out, not_1_out, not_2_out);
  and and_14 (and_14_out, A1, not_7_out);
  xnor xnor_1 (xnor_1_out, in_54, in_58);
  xnor xnor_2 (xnor_2_out, in_55, in_59);
  xnor xnor_3 (xnor_3_out, in_56, in_60);
  xnor xnor_4 (xnor_4_out, in_57, in_61);
  add add_1 (.A(in_67), .B(in_71), .Cin(1'b0), .S(out_108), .Cout(add_1_cout));
  sub sub_1 (.A(in_75), .B(in_79), .Cin(1'b0), .S(out_113), .Cout(sub_1_cout));
  number7decoder number7decoder_1 (
    .num0(in_75), .num1(in_74), .num2(in_73), .num3(in_72), .point(1'b0), .A(number7decoder_1_a),
    .B(number7decoder_1_b), .C(number7decoder_1_c), .D(number7decoder_1_d), .E(number7decoder_1_e),
    .F(number7decoder_1_f), .G(number7decoder_1_g), .H(number7decoder_1_h));
  number7decoder number7decoder_2 (
    .num0(in_79), .num1(in_78), .num2(in_77), .num3(in_76), .point(1'b0), .A(number7decoder_2_a),
    .B(number7decoder_2_b), .C(number7decoder_2_c), .D(number7decoder_2_d), .E(number7decoder_2_e),
    .F(number7decoder_2_f), .G(number7decoder_2_g), .H(number7decoder_2_h));
  number7decoder number7decoder_3 (
    .num0(out_113), .num1(out_112), .num2(out_111), .num3(out_110), .point(1'b0), .A(number7decoder_3_a),
    .B(number7decoder_3_b), .C(number7decoder_3_c), .D(number7decoder_3_d), .E(number7decoder_3_e),
    .F(number7decoder_3_f), .G(number7decoder_3_g), .H(number7decoder_3_h));
  number7decoder number7decoder_4 (
    .num0(in_83), .num1(in_82), .num2(in_81), .num3(in_80), .A(number7decoder_4_a), .B(number7decoder_4_b),
    .C(number7decoder_4_c), .D(number7decoder_4_d), .E(number7decoder_4_e), .F(number7decoder_4_f),
    .G(number7decoder_4_g));  // open: point, H
  number7decoder number7decoder_5 (
    .num0(in_12), .num1(in_13), .num2(in_14), .num3(in_15), .point(in_16), .A(number7decoder_5_a),
    .B(number7decoder_5_b), .C(number7decoder_5_c), .D(number7decoder_5_d), .E(number7decoder_5_e),
    .F(number7decoder_5_f), .G(number7decoder_5_g), .H(number7decoder_5_h));
  encoder16to4 encoder16to4_1 (
    .n0(in_17), .n1(in_18), .n2(in_19), .n3(in_20), .n4(in_21), .n5(in_23), .n6(in_24), .n7(in_25),
    .n8(in_26), .n9(in_27), .na(in_28), .nb(in_29), .nc(in_30), .nd(in_31), .ne(in_32), .nf(in_33),
    .out0(encoder16to4_1_out0), .out1(encoder16to4_1_out1), .out2(encoder16to4_1_out2),
    .out3(encoder16to4_1_out3));
  or or_2 (Y0, and_14_out, A3);
  or or_3 (Y1, A2, A3);
  or or_4 (out_99, and_6_out, and_7_out);
  or or_5 (or_5_out, and_8_out, and_9_out);
  or or_6 (or_6_out, and_10_out, and_11_out);
  and and_15 (out_101, xnor_1_out, xnor_2_out, xnor_3_out, xnor_4_out);
  _7_Segment_Display u_7_segment_display_1 (
    .g(number7decoder_4_g), .f(number7decoder_4_f), .a(number7decoder_4_a), .b(number7decoder_4_b),
    .e(number7decoder_4_e), .d(number7decoder_4_d), .c(number7decoder_4_c));  // open: dp
  decoder2to4 decoder2to4_1 (
    .in0(in_9), .in1(in_10), .out1(decoder2to4_1_out1), .out2(decoder2to4_1_out2), .out3(decoder2to4_1_out3),
    .out4(decoder2to4_1_out4));
  decoder2to4 decoder2to4_2 (
    .in0(in_9), .in1(in_10), .out1(decoder2to4_2_out1), .out2(decoder2to4_2_out2), .out3(decoder2to4_2_out3),
    .out4(decoder2to4_2_out4));
  _7_Segment_Display u_7_segment_display_2 (
    .g(number7decoder_5_g), .f(number7decoder_5_f), .a(number7decoder_5_a), .b(number7decoder_5_b),
    .e(number7decoder_5_e), .d(number7decoder_5_d), .c(number7decoder_5_c), .dp(number7decoder_5_h));
  not not_8 (not_8_out, in_44);
  number7decoder number7decoder_6 (
    .num0(num0), .num1(num1), .num2(num2), .num3(num3), .point(point), .A(number7decoder_6_a),
    .B(number7decoder_6_b), .C(number7decoder_6_c), .D(number7decoder_6_d), .E(number7decoder_6_e),
    .F(number7decoder_6_f), .G(number7decoder_6_g), .H(number7decoder_6_h));
  number7decoderdex number7decoderdex_1 (
    .num0(num0), .num1(num1), .num2(num2), .num3(num3), .point(point), .A(number7decoder_6_c),
    .B(number7decoderdex_1_b), .C(number7decoderdex_1_c), .D(number7decoderdex_1_d),
    .E(number7decoderdex_1_e), .F(number7decoderdex_1_f), .G(number7decoderdex_1_g), .H(number7decoderdex_1_h));
  _7_Segment_Display u_7_segment_display_3 (
    .g(number7decoder_1_g), .f(number7decoder_1_f), .a(number7decoder_1_a), .b(number7decoder_1_b),
    .e(number7decoder_1_e), .d(number7decoder_1_d), .c(number7decoder_1_c), .dp(number7decoder_1_h));
  and and_16 (out_89, not_3_out, decoder2to4_1_out1);
  and and_17 (out_90, not_3_out, decoder2to4_1_out2);
  and and_18 (out_93, decoder2to4_2_out1, in_11);
  and and_19 (out_94, decoder2to4_2_out2, in_11);
  and and_20 (out_95, decoder2to4_2_out3, in_11);
  and and_21 (and_21_out, or_5_out, not_8_out);
  and and_22 (and_22_out, in_44, or_6_out);
  add add_2 (.A(in_66), .B(in_70), .Cin(add_1_cout), .S(out_107), .Cout(add_2_cout));
  sub sub_2 (.A(in_74), .B(in_78), .Cin(sub_1_cout), .S(out_112), .Cout(sub_2_cout));
  not not_9 (not_9_out, in_84);
  _7_Segment_Display u_7_segment_display_4 (.g(1'b1), .b(not_9_out), .c(not_9_out));  // open: f, a, e, d, dp
  _7_Segment_Display u_7_segment_display_5 (.g(1'b1), .f(not_9_out), .e(not_9_out));  // open: a, b, d, c, dp
  and and_23 (out_91, not_3_out, decoder2to4_1_out3);
  and and_24 (out_92, not_3_out, decoder2to4_1_out4);
  and and_25 (out_96, decoder2to4_2_out4, in_11);
  number7decoder number7decoder_7 (
    .num0(encoder16to4_1_out0), .num1(encoder16to4_1_out1), .num2(encoder16to4_1_out2),
    .num3(encoder16to4_1_out3), .point(in_22), .A(number7decoder_7_a), .B(number7decoder_7_b),
    .C(number7decoder_7_c), .D(number7decoder_7_d), .E(number7decoder_7_e), .F(number7decoder_7_f),
    .G(number7decoder_7_g), .H(number7decoder_7_h));
  _7_Segment_Display u_7_segment_display_6 (
    .g(number7decoder_2_g), .f(number7decoder_2_f), .a(number7decoder_2_a), .b(number7decoder_2_b),
    .e(number7decoder_2_e), .d(number7decoder_2_d), .c(number7decoder_2_c), .dp(number7decoder_2_h));
  or or_7 (out_100, and_21_out, and_22_out);
  _7_Segment_Display u_7_segment_display_7 (.g(out_109));  // open: f, a, b, e, d, c, dp
  _7_Segment_Display u_7_segment_display_8 (
    .g(number7decoder_3_g), .f(number7decoder_3_f), .a(number7decoder_3_a), .b(number7decoder_3_b),
    .e(number7decoder_3_e), .d(number7decoder_3_d), .c(number7decoder_3_c), .dp(number7decoder_3_h));
  _7_Segment_Display u_7_segment_display_9 (
    .g(number7decoder_8_g), .f(number7decoder_8_f), .a(number7decoder_8_a), .b(number7decoder_8_b),
    .e(number7decoder_8_e), .d(number7decoder_8_d), .c(number7decoder_8_c));  // open: dp
  number7decoder number7decoder_8 (
    .num0(in_88), .num1(in_87), .num2(in_86), .num3(in_85), .A(number7decoder_8_a), .B(number7decoder_8_b),
    .C(number7decoder_8_c), .D(number7decoder_8_d), .E(number7decoder_8_e), .F(number7decoder_8_f),
    .G(number7decoder_8_g));  // open: point, H
  _7_Segment_Display u_7_segment_display_10 (
    .g(number7decoder_7_g), .f(number7decoder_7_f), .a(number7decoder_7_a), .b(number7decoder_7_b),
    .e(number7decoder_7_e), .d(number7decoder_7_d), .c(number7decoder_7_c), .dp(number7decoder_7_h));
  add add_3 (.A(in_65), .B(in_69), .Cin(add_2_cout), .S(out_106), .Cout(add_3_cout));
  sub sub_3 (.A(in_73), .B(in_77), .Cin(sub_2_cout), .S(out_111), .Cout(sub_3_cout));
  add4bit add4bit_1 (
    .A3(in_80), .A2(in_81), .A1(in_82), .A0(in_83), .B3(in_85), .B2(in_86), .B1(in_87), .B0(in_88),
    .C(add4bit_1_c), .S3(add4bit_1_s3), .S2(add4bit_1_s2), .S1(add4bit_1_s1), .S0(add4bit_1_s0));
  sub4bitorigin sub4bitorigin_1 (
    .A3(in_80), .A2(in_81), .A1(in_82), .A0(in_83), .B3(in_85), .B2(in_86), .B1(in_87), .B0(in_88),
    .sign(sub4bitorigin_1_sign), .S3(sub4bitorigin_1_s3), .S2(sub4bitorigin_1_s2), .S1(sub4bitorigin_1_s1),
    .S0(sub4bitorigin_1_s0));
  and and_26 (and_26_out, sub4bitorigin_1_sign, in_84);
  _7_Segment_Display u_7_segment_display_11 (.g(1'b1), .d(1'b1));  // open: f, a, b, e, c, dp
  bit1select2 bit1select2_1 (
    .in0(number7decoder_6_a), .sel(switch), .in1(number7decoder_6_c), .out0(bit1select2_1_out0));
  bit1select2 bit1select2_2 (
    .in0(number7decoder_6_b), .sel(switch), .in1(number7decoderdex_1_b), .out0(bit1select2_2_out0));
  bit1select2 bit1select2_3 (
    .in0(number7decoder_6_c), .sel(switch), .in1(number7decoderdex_1_c), .out0(bit1select2_3_out0));
  bit1select2 bit1select2_4 (
    .in0(number7decoder_6_d), .sel(switch), .in1(number7decoderdex_1_d), .out0(bit1select2_4_out0));
  bit1select2 bit1select2_5 (
    .in0(number7decoder_6_e), .sel(switch), .in1(number7decoderdex_1_e), .out0(bit1select2_5_out0));
  bit1select2 bit1select2_6 (
    .in0(number7decoder_6_f), .sel(switch), .in1(number7decoderdex_1_f), .out0(bit1select2_6_out0));
  bit1select2 bit1select2_7 (
    .in0(number7decoder_6_g), .sel(switch), .in1(number7decoderdex_1_g), .out0(bit1select2_7_out0));
  bit1select2 bit1select2_8 (
    .in0(number7decoder_6_h), .sel(switch), .in1(number7decoderdex_1_h), .out0(bit1select2_8_out0));
  _7_Segment_Display u_7_segment_display_12 (.g(and_26_out));  // open: f, a, b, e, d, c, dp
  add add_4 (.A(in_64), .B(in_68), .Cin(add_3_cout), .S(out_105), .Cout(out_104));
  sub sub_4 (.A(in_72), .B(in_76), .Cin(sub_3_cout), .S(out_110), .Cout(out_109));
  _7_Segment_Display u_7_segment_display_13 (
    .g(number7decoder_9_g), .f(number7decoder_9_f), .a(number7decoder_9_a), .b(number7decoder_9_b),
    .e(number7decoder_9_e), .d(number7decoder_9_d), .c(number7decoder_9_c));  // open: dp
  _7_Segment_Display u_7_segment_display_14 (
    .g(bit1select2_7_out0), .f(bit1select2_6_out0), .a(bit1select2_1_out0), .b(bit1select2_2_out0),
    .e(bit1select2_5_out0), .d(bit1select2_4_out0), .c(bit1select2_3_out0), .dp(bit1select2_8_out0));
  bit1select2for4bit bit1select2for4bit_1 (
    .A3(add4bit_1_s3), .A2(add4bit_1_s2), .A1(add4bit_1_s1), .A0(add4bit_1_s0), .B3(sub4bitorigin_1_s3),
    .B2(sub4bitorigin_1_s2), .B1(sub4bitorigin_1_s1), .B0(sub4bitorigin_1_s0), .Sel(in_84),
    .out3(bit1select2for4bit_1_out3), .out2(bit1select2for4bit_1_out2), .out1(bit1select2for4bit_1_out1),
    .out0(bit1select2for4bit_1_out0));
  LED led_4 (.in(and_27_out));
  and and_27 (and_27_out, add4bit_1_c, not_9_out);
  number7decoder number7decoder_9 (
    .num0(bit1select2for4bit_1_out0), .num1(bit1select2for4bit_1_out1), .num2(bit1select2for4bit_1_out2),
    .num3(bit1select2for4bit_1_out3), .A(number7decoder_9_a), .B(number7decoder_9_b), .C(number7decoder_9_c),
    .D(number7decoder_9_d), .E(number7decoder_9_e), .F(number7decoder_9_f), .G(number7decoder_9_g));  // open: point, H

  // Notes on the sheet:
  //   3-8译码器
  //   16-4译码器接数码管
  //   7段数码管
  //   4-2优先编码器
  //   1位2选1选择器
  //   3位4选1选择器
  //   10/16进制选择数码管
  //   4位比较器
  //   1位全加器
  //   4位全加器
  //   4位减法器
  //   4位原码加减法器
  //   C
  //   C
  //   -
  //   =
  //   溢出：
endmodule

module decoder2to4 (
  input  in0,
  input  in1,
  output out1,
  output out2,
  output out3,
  output out4
);

  wire not_1_out, not_2_out;

  not not_1 (not_1_out, in1);
  not not_2 (not_2_out, in0);
  and and_1 (out4, in1, in0);
  and and_2 (out3, in1, not_2_out);
  and and_3 (out2, not_1_out, in0);
  and and_4 (out1, not_1_out, not_2_out);
endmodule

module number7decoder (
  input  num0,
  input  num1,
  input  num2,
  input  num3,
  input  point,
  output A,
  output B,
  output C,
  output D,
  output E,
  output F,
  output G,
  output H
);

  wire n0_out, n1_out, n2_out, n3_out, n4_out, n5_out, n6_out, n7_out, n8_out, n9_out, na_out, nb_out,
       nc_out, nd_out, ne_out, nf_out, not_1_out, not_2_out, not_3_out, not_4_out;

  not not_1 (not_1_out, num0);
  not not_2 (not_2_out, num1);
  not not_3 (not_3_out, num2);
  not not_4 (not_4_out, num3);
  and nf (nf_out, num3, num2, num1, num0);
  or or_1 (A, n0_out, n2_out, n3_out, n5_out, n6_out, n7_out, n8_out, n9_out, na_out, nc_out, ne_out, nf_out);
  and ne (ne_out, num3, num2, num1, not_1_out);
  and nd (nd_out, num3, num2, not_2_out, num0);
  and nc (nc_out, num3, num2, not_2_out, not_1_out);
  or or_2 (B, n0_out, n1_out, n2_out, n3_out, n4_out, n7_out, n8_out, n9_out, na_out, nd_out);
  and nb (nb_out, num3, not_3_out, num1, num0);
  and na (na_out, num3, not_3_out, num1, not_1_out);
  and n9 (n9_out, num3, not_3_out, not_2_out, num0);
  or or_3 (C, n0_out, n1_out, n3_out, n4_out, n5_out, n6_out, n7_out, n8_out, n9_out, na_out, nb_out, nd_out);
  and n8 (n8_out, num3, not_3_out, not_2_out, not_1_out);
  or or_4 (D, n0_out, n2_out, n3_out, n5_out, n6_out, n8_out, n9_out, nb_out, nc_out, nd_out, ne_out);
  and n7 (n7_out, not_4_out, num2, num1, num0);
  and n6 (n6_out, not_4_out, num2, num1, not_1_out);
  and n5 (n5_out, not_4_out, num2, not_2_out, num0);
  or or_5 (E, n0_out, n2_out, n6_out, n8_out, na_out, nb_out, nc_out, nd_out, ne_out, nf_out);
  and n4 (n4_out, not_4_out, num2, not_2_out, not_1_out);
  and n3 (n3_out, not_4_out, not_3_out, num1, num0);
  or or_6 (F, n0_out, n4_out, n5_out, n6_out, n8_out, n9_out, na_out, nb_out, nc_out, ne_out, nf_out);
  and n1 (n1_out, not_4_out, not_3_out, not_2_out, num0);
  and n2 (n2_out, not_4_out, not_3_out, num1, not_1_out);
  or or_7 (G, n2_out, n3_out, n4_out, n5_out, n6_out, n8_out, n9_out, na_out, nb_out, nd_out, ne_out, nf_out);
  and n0 (n0_out, not_4_out, not_3_out, not_2_out, not_1_out);

  assign H = point;
endmodule

module encoder16to4 (
  input  n0,
  input  n1,
  input  n2,
  input  n3,
  input  n4,
  input  n5,
  input  n6,
  input  n7,
  input  n8,
  input  n9,
  input  na,
  input  nb,
  input  nc,
  input  nd,
  input  ne,
  input  nf,
  output out0,
  output out1,
  output out2,
  output out3
);

  or or_1 (out3, n8, n9, na, nb, nc, nd, ne, nf);
  or or_2 (out1, n2, n3, n6, n7, na, nb, ne, nf);
  or or_3 (out2, n4, n5, n6, n7, nc, nd, ne, nf);
  or or_4 (out0, n1, n3, n5, n7, n9, nb, nd, nf);
endmodule

module number7decoderdex (
  input  num0,
  input  num1,
  input  num2,
  input  num3,
  input  point,
  output A,
  output B,
  output C,
  output D,
  output E,
  output F,
  output G,
  output H
);

  wire n0_out, n1_out, n2_out, n3_out, n4_out, n5_out, n6_out, n7_out, n8_out, n9_out, na_out, nb_out,
       nc_out, nd_out, ne_out, nf_out, not_1_out, not_2_out, not_3_out, not_4_out;

  or or_1 (H, point, nf_out, ne_out, nd_out, nc_out, nb_out, na_out);
  not not_1 (not_1_out, num0);
  not not_2 (not_2_out, num1);
  not not_3 (not_3_out, num2);
  not not_4 (not_4_out, num3);
  and nf (nf_out, num3, num2, num1, num0);
  or or_2 (A, n0_out, n2_out, n3_out, n5_out, n6_out, n7_out, n8_out, n9_out, 1'b0, 1'b0, 1'b0, 1'b0);
  and ne (ne_out, num3, num2, num1, not_1_out);
  and nd (nd_out, num3, num2, not_2_out, num0);
  and nc (nc_out, num3, num2, not_2_out, not_1_out);
  or or_3 (B, n0_out, n1_out, n2_out, n3_out, n4_out, n7_out, n8_out, n9_out, 1'b0, 1'b0);
  and nb (nb_out, num3, not_3_out, num1, num0);
  and na (na_out, num3, not_3_out, num1, not_1_out);
  and n9 (n9_out, num3, not_3_out, not_2_out, num0);
  or or_4 (C, n0_out, n1_out, n3_out, n4_out, n5_out, n6_out, n7_out, n8_out, n9_out, 1'b0, 1'b0, 1'b0);
  and n8 (n8_out, num3, not_3_out, not_2_out, not_1_out);
  or or_5 (D, n0_out, n2_out, n3_out, n5_out, n6_out, n8_out, n9_out, 1'b0, 1'b0, 1'b0, 1'b0);
  and n7 (n7_out, not_4_out, num2, num1, num0);
  and n6 (n6_out, not_4_out, num2, num1, not_1_out);
  and n5 (n5_out, not_4_out, num2, not_2_out, num0);
  or or_6 (E, n0_out, n2_out, n6_out, n8_out, 1'b0, 1'b0, 1'b0, 1'b0, 1'b0, 1'b0);
  and n4 (n4_out, not_4_out, num2, not_2_out, not_1_out);
  and n3 (n3_out, not_4_out, not_3_out, num1, num0);
  or or_7 (F, n0_out, n4_out, n5_out, n6_out, n8_out, n9_out, 1'b0, 1'b0, 1'b0, 1'b0, 1'b0);
  and n1 (n1_out, not_4_out, not_3_out, not_2_out, num0);
  and n2 (n2_out, not_4_out, not_3_out, num1, not_1_out);
  or or_8 (G, n2_out, n3_out, n4_out, n5_out, n6_out, n8_out, n9_out, 1'b0, 1'b0, 1'b0, 1'b0, 1'b0);
  and n0 (n0_out, not_4_out, not_3_out, not_2_out, not_1_out);
endmodule

module bit1select2 (
  input  in0,
  input  sel,
  input  in1,
  output out0
);

  wire and_1_out, and_2_out, not_1_out;

  not not_1 (not_1_out, sel);
  and and_1 (and_1_out, in0, not_1_out);
  and and_2 (and_2_out, sel, in1);
  or or_1 (out0, and_1_out, and_2_out);
endmodule

module add (
  input  A,
  input  B,
  input  Cin,
  output S,
  output Cout
);

  wire and_1_out, and_2_out, xor_1_out;

  xor xor_1 (xor_1_out, A, B);
  and and_1 (and_1_out, A, B);
  xor xor_2 (S, xor_1_out, Cin);
  and and_2 (and_2_out, xor_1_out, Cin);
  or or_1 (Cout, and_2_out, and_1_out);
endmodule

module sub (
  input  A,
  input  B,
  input  Cin,
  output S,
  output Cout
);

  wire and_1_out, and_2_out, and_3_out, and_4_out, not_1_out, not_2_out, or_1_out, xnor_1_out, xor_1_out;

  not not_1 (not_1_out, A);
  not not_2 (not_2_out, Cin);
  or or_1 (or_1_out, not_1_out, B);
  xor xor_1 (xor_1_out, A, B);
  xnor xnor_1 (xnor_1_out, A, B);
  and and_1 (and_1_out, not_1_out, B);
  and and_2 (and_2_out, or_1_out, Cin);
  and and_3 (and_3_out, xor_1_out, not_2_out);
  or or_2 (S, and_3_out, and_4_out);
  and and_4 (and_4_out, Cin, xnor_1_out);
  or or_3 (Cout, and_1_out, and_2_out);
endmodule

module add4bit (
  input  A3,
  input  A2,
  input  A1,
  input  A0,
  input  B3,
  input  B2,
  input  B1,
  input  B0,
  output C,
  output S3,
  output S2,
  output S1,
  output S0
);

  wire add_1_cout, add_2_cout, add_3_cout;

  add add_1 (.A(A0), .B(B0), .Cin(1'b0), .S(S0), .Cout(add_1_cout));
  add add_2 (.A(A1), .B(B1), .Cin(add_1_cout), .S(S1), .Cout(add_2_cout));
  add add_3 (.A(A2), .B(B2), .Cin(add_2_cout), .S(S2), .Cout(add_3_cout));
  add add_4 (.A(A3), .B(B3), .Cin(add_3_cout), .S(S3), .Cout(C));

  // Notes on the sheet:
  //   +
  //   =
endmodule

module sub4bit (
  input  A3,
  input  A2,
  input  A1,
  input  A0,
  input  B3,
  input  B2,
  input  B1,
  input  B0,
  output C,
  output S3,
  output S2,
  output S1,
  output S0
);

  wire sub_1_cout, sub_2_cout, sub_3_cout;

  sub sub_1 (.A(A0), .B(B0), .Cin(1'b0), .S(S0), .Cout(sub_1_cout));
  sub sub_2 (.A(A1), .B(B1), .Cin(sub_1_cout), .S(S1), .Cout(sub_2_cout));
  sub sub_3 (.A(A2), .B(B2), .Cin(sub_2_cout), .S(S2), .Cout(sub_3_cout));
  sub sub_4 (.A(A3), .B(B3), .Cin(sub_3_cout), .S(S3), .Cout(C));

  // Notes on the sheet:
  //   +
  //   =
endmodule

module sub4bitorigin (
  input  A3,
  input  A2,
  input  A1,
  input  A0,
  input  B3,
  input  B2,
  input  B1,
  input  B0,
  output sign,
  output S3,
  output S2,
  output S1,
  output S0
);

  wire add4bit_1_s0, add4bit_1_s1, add4bit_1_s2, add4bit_1_s3, not_1_out, not_2_out, not_3_out, not_4_out,
       sub4bit_1_s0, sub4bit_1_s1, sub4bit_1_s2, sub4bit_1_s3;

  sub4bit sub4bit_1 (
    .A3(A3), .A2(A2), .A1(A1), .A0(A0), .B3(B3), .B2(B2), .B1(B1), .B0(B0), .C(sign), .S3(sub4bit_1_s3),
    .S2(sub4bit_1_s2), .S1(sub4bit_1_s1), .S0(sub4bit_1_s0));
  not not_1 (not_1_out, sub4bit_1_s3);
  not not_2 (not_2_out, sub4bit_1_s2);
  not not_3 (not_3_out, sub4bit_1_s1);
  not not_4 (not_4_out, sub4bit_1_s0);
  add4bit add4bit_1 (
    .A3(not_1_out), .A2(not_2_out), .A1(not_3_out), .A0(not_4_out), .B3(1'b0), .B2(1'b0), .B1(1'b0),
    .B0(1'b1), .S3(add4bit_1_s3), .S2(add4bit_1_s2), .S1(add4bit_1_s1), .S0(add4bit_1_s0));  // open: C
  bit1select2for4bit bit1select2for4bit_1 (
    .A3(sub4bit_1_s3), .A2(sub4bit_1_s2), .A1(sub4bit_1_s1), .A0(sub4bit_1_s0), .B3(add4bit_1_s3),
    .B2(add4bit_1_s2), .B1(add4bit_1_s1), .B0(add4bit_1_s0), .Sel(sign), .out3(S3), .out2(S2), .out1(S1),
    .out0(S0));
endmodule

module bit1select2for4bit (
  input  A3,
  input  A2,
  input  A1,
  input  A0,
  input  B3,
  input  B2,
  input  B1,
  input  B0,
  input  Sel,
  output out3,
  output out2,
  output out1,
  output out0
);

  bit1select2 bit1select2_1 (.in0(A3), .sel(Sel), .in1(B3), .out0(out3));
  bit1select2 bit1select2_2 (.in0(A2), .sel(Sel), .in1(B2), .out0(out2));
  bit1select2 bit1select2_3 (.in0(A1), .sel(Sel), .in1(B1), .out0(out1));
  bit1select2 bit1select2_4 (.in0(A0), .sel(Sel), .in1(B0), .out0(out0));
endmodule

module SR (
  input  S,
  input  R,
  output Q,
  output NQ
);

  nor nor_1 (Q, S, NQ);
  nor nor_2 (NQ, Q, R);
endmodule

module Dlatch (
  input  rst,
  input  WE,
  input  D,
  output Q,
  output NQ
);

  wire and_1_out, and_2_out, bit1select2_1_out0, bit1select2_2_out0, not_1_out;

  not not_1 (not_1_out, D);
  and and_1 (and_1_out, WE, D);
  and and_2 (and_2_out, not_1_out, WE);
  bit1select2 bit1select2_1 (.in0(and_1_out), .sel(rst), .in1(1'b1), .out0(bit1select2_1_out0));
  bit1select2 bit1select2_2 (.in0(and_2_out), .sel(rst), .in1(1'b0), .out0(bit1select2_2_out0));
  SR sr_1 (.S(bit1select2_1_out0), .R(bit1select2_2_out0), .Q(Q), .NQ(NQ));
endmodule

module Dtrigger (
  input  EN,
  input  clk,
  input  D,
  input  rst,
  output Q
);

  wire and_1_out, dlatch_1_q, not_1_out;

  and and_1 (and_1_out, EN, clk);
  not not_1 (not_1_out, and_1_out);
  Dlatch dlatch_1 (.WE(not_1_out), .D(D), .Q(dlatch_1_q));  // open: rst, NQ
  Dlatch dlatch_2 (.rst(rst), .WE(and_1_out), .D(dlatch_1_q), .Q(Q));  // open: NQ
endmodule

module bit4register (
  input  rst,
  input  num3,
  input  num2,
  input  num1,
  input  num0,
  input  EN,
  input  clk,
  output out3,
  output out2,
  output out1,
  output out0
);

  Dtrigger dtrigger_1 (.EN(EN), .clk(clk), .D(num3), .rst(rst), .Q(out3));
  Dtrigger dtrigger_2 (.EN(EN), .clk(clk), .D(num2), .rst(rst), .Q(out2));
  Dtrigger dtrigger_3 (.EN(EN), .clk(clk), .D(num1), .rst(rst), .Q(out1));
  Dtrigger dtrigger_4 (.EN(EN), .clk(clk), .D(num0), .rst(rst), .Q(out0));
endmodule

module bit8register (
  input  rst,
  input  num7,
  input  num6,
  input  num5,
  input  num4,
  input  num3,
  input  num2,
  input  num1,
  input  num0,
  input  clk,
  input  EN,
  output out7,
  output out6,
  output out5,
  output out4,
  output out3,
  output out2,
  output out1,
  output out0
);

  bit4register bit4register_1 (
    .rst(rst), .num3(num7), .num2(num6), .num1(num5), .num0(num4), .EN(EN), .clk(clk), .out3(out7),
    .out2(out6), .out1(out5), .out0(out4));
  bit4register bit4register_2 (
    .rst(rst), .num3(num3), .num2(num2), .num1(num1), .num0(num0), .EN(EN), .clk(clk), .out3(out3),
    .out2(out2), .out1(out1), .out0(out0));
endmodule

module add8bit (
  input  A7,
  input  A6,
  input  A5,
  input  A4,
  input  A3,
  input  A2,
  input  A1,
  input  A0,
  input  B7,
  input  B6,
  input  B5,
  input  B4,
  input  B3,
  input  B2,
  input  B1,
  input  B0,
  output S7,
  output S6,
  output S5,
  output S4,
  output S3,
  output S2,
  output S1,
  output S0,
  output C
);

  wire add_2_cout, add_3_cout, add_4_cout, add_5_cout, add_6_cout, add_7_cout, add_8_cout;

  add add_1 (.A(A7), .B(B7), .Cin(add_2_cout), .S(S7), .Cout(C));
  add add_2 (.A(A6), .B(B6), .Cin(add_3_cout), .S(S6), .Cout(add_2_cout));
  add add_3 (.A(A5), .B(B5), .Cin(add_4_cout), .S(S5), .Cout(add_3_cout));
  add add_4 (.A(A4), .B(B4), .Cin(add_5_cout), .S(S4), .Cout(add_4_cout));
  add add_5 (.A(A3), .B(B3), .Cin(add_6_cout), .S(S3), .Cout(add_5_cout));
  add add_6 (.A(A2), .B(B2), .Cin(add_7_cout), .S(S2), .Cout(add_6_cout));
  add add_7 (.A(A1), .B(B1), .Cin(add_8_cout), .S(S1), .Cout(add_7_cout));
  add add_8 (.A(A0), .B(B0), .Cin(1'b0), .S(S0), .Cout(add_8_cout));
endmodule

module couter8bit (
  input  clk,
  input  EN,
  input  rst
);

  wire add8bit_1_s0, add8bit_1_s1, add8bit_1_s2, add8bit_1_s3, add8bit_1_s4, add8bit_1_s5, add8bit_1_s6,
       add8bit_1_s7, bit8register_1_out0, bit8register_1_out1, bit8register_1_out2, bit8register_1_out3,
       bit8register_1_out4, bit8register_1_out5, bit8register_1_out6, bit8register_1_out7,
       bit8register_2_out0, bit8register_2_out1, bit8register_2_out2, bit8register_2_out3,
       bit8register_2_out4, bit8register_2_out5, bit8register_2_out6, bit8register_2_out7, not_1_out,
       number7decoder_1_a, number7decoder_1_b, number7decoder_1_c, number7decoder_1_d, number7decoder_1_e,
       number7decoder_1_f, number7decoder_1_g, number7decoder_2_a, number7decoder_2_b, number7decoder_2_c,
       number7decoder_2_d, number7decoder_2_e, number7decoder_2_f, number7decoder_2_g;

  not not_1 (not_1_out, clk);
  bit8register bit8register_1 (
    .rst(rst), .num7(bit8register_2_out7), .num6(bit8register_2_out6), .num5(bit8register_2_out5),
    .num4(bit8register_2_out4), .num3(bit8register_2_out3), .num2(bit8register_2_out2),
    .num1(bit8register_2_out1), .num0(bit8register_2_out0), .clk(clk), .EN(EN), .out7(bit8register_1_out7),
    .out6(bit8register_1_out6), .out5(bit8register_1_out5), .out4(bit8register_1_out4),
    .out3(bit8register_1_out3), .out2(bit8register_1_out2), .out1(bit8register_1_out1),
    .out0(bit8register_1_out0));
  add8bit add8bit_1 (
    .A7(bit8register_1_out7), .A6(bit8register_1_out6), .A5(bit8register_1_out5), .A4(bit8register_1_out4),
    .A3(bit8register_1_out3), .A2(bit8register_1_out2), .A1(bit8register_1_out1), .A0(bit8register_1_out0),
    .B7(1'b0), .B6(1'b0), .B5(1'b0), .B4(1'b0), .B3(1'b0), .B2(1'b0), .B1(1'b0), .B0(1'b1),
    .S7(add8bit_1_s7), .S6(add8bit_1_s6), .S5(add8bit_1_s5), .S4(add8bit_1_s4), .S3(add8bit_1_s3),
    .S2(add8bit_1_s2), .S1(add8bit_1_s1), .S0(add8bit_1_s0));  // open: C
  _7_Segment_Display u_7_segment_display_1 (
    .g(number7decoder_1_g), .f(number7decoder_1_f), .a(number7decoder_1_a), .b(number7decoder_1_b),
    .e(number7decoder_1_e), .d(number7decoder_1_d), .c(number7decoder_1_c));  // open: dp
  bit8register bit8register_2 (
    .rst(rst), .num7(add8bit_1_s7), .num6(add8bit_1_s6), .num5(add8bit_1_s5), .num4(add8bit_1_s4),
    .num3(add8bit_1_s3), .num2(add8bit_1_s2), .num1(add8bit_1_s1), .num0(add8bit_1_s0), .clk(not_1_out),
    .EN(EN), .out7(bit8register_2_out7), .out6(bit8register_2_out6), .out5(bit8register_2_out5),
    .out4(bit8register_2_out4), .out3(bit8register_2_out3), .out2(bit8register_2_out2),
    .out1(bit8register_2_out1), .out0(bit8register_2_out0));
  _7_Segment_Display u_7_segment_display_2 (
    .g(number7decoder_2_g), .f(number7decoder_2_f), .a(number7decoder_2_a), .b(number7decoder_2_b),
    .e(number7decoder_2_e), .d(number7decoder_2_d), .c(number7decoder_2_c));  // open: dp
  number7decoder number7decoder_1 (
    .num0(bit8register_2_out4), .num1(bit8register_2_out5), .num2(bit8register_2_out6),
    .num3(bit8register_2_out7), .A(number7decoder_1_a), .B(number7decoder_1_b), .C(number7decoder_1_c),
    .D(number7decoder_1_d), .E(number7decoder_1_e), .F(number7decoder_1_f), .G(number7decoder_1_g));  // open: point, H
  number7decoder number7decoder_2 (
    .num0(bit8register_2_out0), .num1(bit8register_2_out1), .num2(bit8register_2_out2),
    .num3(bit8register_2_out3), .A(number7decoder_2_a), .B(number7decoder_2_b), .C(number7decoder_2_c),
    .D(number7decoder_2_d), .E(number7decoder_2_e), .F(number7decoder_2_f), .G(number7decoder_2_g));  // open: point, H
endmodule

module arraySumCalculator (
  input  EN,
  input  clk,
  input  rst
);

  wire not_1_out;
  wire [7:0] adder_1_out, adder_2_out, register_1_q, register_2_q, register_3_q;

  Register register_1 (.D(register_2_q), .en(EN), .clk(clk), .Q(register_1_q), .clr(rst));
  not not_1 (not_1_out, clk);
  Adder adder_1 (.a(register_3_q), .b(register_1_q), .out(adder_1_out));  // open: cin, cout
  Register register_2 (.D(adder_2_out), .en(EN), .clk(not_1_out), .Q(register_2_q), .clr(rst));
  Adder adder_2 (.a(register_1_q), .b(8'h1), .out(adder_2_out));  // open: cin, cout
  Register register_3 (.D(adder_1_out), .en(EN), .clk(clk), .Q(register_3_q), .clr(rst));
  Hex_Digit_Display hex_digit_display_1 (.value(register_1_q[7:4]));  // open: dp
  Hex_Digit_Display hex_digit_display_2 (.value(register_3_q[7:4]));  // open: dp
  Hex_Digit_Display hex_digit_display_3 (.value(register_1_q[3:0]));  // open: dp
  Hex_Digit_Display hex_digit_display_4 (.value(register_3_q[3:0]));  // open: dp

  // Notes on the sheet:
  //   N
  //   前N-1项和
  //   N+1
endmodule

module electricClock (
  input  rst,
  input  EN
);

  wire clk_out, comparator_1_eq, comparator_2_eq, comparator_3_eq, comparator_4_eq, or_1_out, or_2_out,
       or_3_out, or_4_out;
  wire [7:0] adder_1_out, adder_2_out, adder_3_out, adder_4_out, register_1_q, register_2_q, register_3_q,
       register_4_q;

  Clock clk (.out(clk_out));
  Register register_1 (.D(adder_1_out), .en(EN), .clk(clk_out), .Q(register_1_q), .clr(or_1_out));
  or or_1 (or_1_out, rst, comparator_1_eq);
  Register register_2 (.D(adder_2_out), .en(EN), .clk(comparator_1_eq), .Q(register_2_q), .clr(or_2_out));
  or or_2 (or_2_out, rst, comparator_2_eq);
  Register register_3 (.D(adder_3_out), .en(EN), .clk(comparator_2_eq), .Q(register_3_q), .clr(or_3_out));
  or or_3 (or_3_out, rst, comparator_3_eq);
  Register register_4 (.D(adder_4_out), .en(EN), .clk(comparator_3_eq), .Q(register_4_q), .clr(or_4_out));
  or or_4 (or_4_out, rst, comparator_4_eq);
  Adder adder_1 (.a(register_1_q), .b(8'h1), .out(adder_1_out));  // open: cin, cout
  Adder adder_2 (.a(register_2_q), .b(8'h1), .out(adder_2_out));  // open: cin, cout
  Adder adder_3 (.a(register_3_q), .b(8'h1), .out(adder_3_out));  // open: cin, cout
  Adder adder_4 (.a(register_4_q), .b(8'h1), .out(adder_4_out));  // open: cin, cout
  Comparator comparator_1 (.a(register_1_q), .b(8'ha), .eq(comparator_1_eq));  // open: gt, lt
  Comparator comparator_2 (.a(register_2_q), .b(8'h6), .eq(comparator_2_eq));  // open: gt, lt
  Comparator comparator_3 (.a(register_3_q), .b(8'ha), .eq(comparator_3_eq));  // open: gt, lt
  Comparator comparator_4 (.a(register_4_q), .b(8'h6), .eq(comparator_4_eq));  // open: gt, lt
  Hex_Digit_Display hex_digit_display_1 (.value(register_4_q[3:0]));  // open: dp
  Hex_Digit_Display hex_digit_display_2 (.value(register_3_q[3:0]));  // open: dp
  Hex_Digit_Display hex_digit_display_3 (.value(register_2_q[3:0]));  // open: dp
  Hex_Digit_Display hex_digit_display_4 (.value(register_1_q[3:0]));  // open: dp

  // Notes on the sheet:
  //   minute
  //   second
endmodule
