// Logisim project F6.circ as structural Verilog: 8 circuits, main circuit main
module main (
  input  EN,
  input  rst
);

  wire and_2_out, and_3_out, clk_out, comparator_1_lt, comparator_2_gt, controller_1_pcselect,
       controller_1_rmen, controller_1_wdselect, controller_1_wmen, controller_1_wordls, controller_1_wren,
       memory_1_byte0en, memory_1_byte1en, memory_1_byte2en, memory_1_byte3en, nor_1_out, not_1_out,
       or_1_out, rgb_video_1_p3;
  wire [1:0] controller_1_aluselect;
  wire [2:0] controller_1_insttype;
  wire [7:0] memory_1_writeout, rgb_video_1_p4, rgb_video_1_p5;
  wire [15:0] memory_1_adressword;
  wire [23:0] pc_1_pc_out, rgb_video_1_p6;
  wire [31:0] alu_1_c, immediate_1_imm, memory_1_dataout, multiplexer_1_out, multiplexer_2_out,
       pc_1_pc_next_out, ram_1_dout, registers_1_rs1d, registers_1_rs2d, rom_1_data;
  wire [31:24] pc_1_pc_out_2;

  Clock clk (.out(clk_out));
  // RGB_Video #(.height(256), .width(256)) rgb_video_1: pin names not known; wires that end beside it: rst, clk_out, rgb_video_1_p3, rgb_video_1_p4, rgb_video_1_p5, rgb_video_1_p6
  and and_1 (rgb_video_1_p3, and_2_out, nor_1_out);
  ROM #(.addrWidth(24), .dataWidth(32)) rom_1 (.addr(pc_1_pc_out), .data(rom_1_data));
  PC pc_1 (
    .PC_in(alu_1_c), .PC_select(controller_1_pcselect), .EN(EN), .clk(clk_out), .rst(rst),
    .PC_out({pc_1_pc_out_2, pc_1_pc_out}), .PC_next_out(pc_1_pc_next_out));
  Comparator #(.mode("unsigned"), .width(32)) comparator_1 (
    .a({memory_1_adressword, rgb_video_1_p5, rgb_video_1_p4}), .b(32'h8000000), .lt(comparator_1_lt));  // open: gt, eq
  Comparator #(.mode("unsigned"), .width(32)) comparator_2 (
    .a({memory_1_adressword, rgb_video_1_p5, rgb_video_1_p4}), .b(32'h8010000), .gt(comparator_2_gt));  // open: eq, lt
  and and_2 (and_2_out, controller_1_wordls, controller_1_wmen);
  nor nor_1 (nor_1_out, comparator_1_lt, comparator_2_gt);
  or or_1 (or_1_out, controller_1_rmen, controller_1_wmen);
  Memory memory_1 (
    .wordLS(controller_1_wordls), .adress(alu_1_c), .adressValid(or_1_out), .dataIn(registers_1_rs2d),
    .readIn(ram_1_dout), .byte3EN(memory_1_byte3en), .byte2EN(memory_1_byte2en), .byte1EN(memory_1_byte1en),
    .byte0EN(memory_1_byte0en), .adressWord({memory_1_adressword, rgb_video_1_p5, rgb_video_1_p4}),
    .writeOut({memory_1_writeout, rgb_video_1_p6}), .dataOut(memory_1_dataout));
  not not_1 (not_1_out, nor_1_out);
  Controller controller_1 (
    .opcode(rom_1_data[6:0]), .funct3(rom_1_data[14:12]), .funct7(rom_1_data[31:25]),
    .ALUSelect(controller_1_aluselect), .pcSelect(controller_1_pcselect), .instType(controller_1_insttype),
    .wDSelect(controller_1_wdselect), .wREN(controller_1_wren), .wMEN(controller_1_wmen),
    .rMEN(controller_1_rmen), .wordLS(controller_1_wordls));
  and and_3 (and_3_out, not_1_out, controller_1_wmen);
  RAM #(.addrWidth(24), .asyncread("true"), .byteenables("byteEnables"), .dataWidth(32), .\type ("nonvolatile")) ram_1 (
    .addr({memory_1_adressword[7:0], rgb_video_1_p5, rgb_video_1_p4}), .we(and_3_out), .oe(1'b1),
    .clk(clk_out), .din({memory_1_writeout, rgb_video_1_p6}), .dout(ram_1_dout), .be3(memory_1_byte3en),
    .be2(memory_1_byte2en), .be1(memory_1_byte1en), .be0(memory_1_byte0en));
  Multiplexer #(.width(32)) multiplexer_1 (
    .in0(multiplexer_2_out), .in1(pc_1_pc_next_out), .out(multiplexer_1_out), .sel(controller_1_wdselect));
  Immediate immediate_1 (.instType(controller_1_insttype), .instruction(rom_1_data), .imm(immediate_1_imm));
  Registers registers_1 (
    .clk(clk_out), .rst(rst), .rdR(rom_1_data[10:7]), .rdD(multiplexer_1_out), .wEN(controller_1_wren),
    .rs1R(rom_1_data[18:15]), .rs2R(rom_1_data[23:20]), .rs1D(registers_1_rs1d), .rs2D(registers_1_rs2d));
  Multiplexer #(.width(32)) multiplexer_2 (
    .in0(alu_1_c), .in1(memory_1_dataout), .out(multiplexer_2_out), .sel(controller_1_rmen));
  ALU alu_1 (
    .ALUSelect(controller_1_aluselect), .A(registers_1_rs1d), .imm(immediate_1_imm), .B(registers_1_rs2d),
    .C(alu_1_c));

  // Notes on the sheet:
  //   RV32I with 16 registers and Inst: add, addi, lui, lw, lbu, sw, sb, jalr
  //   contents of rom_1 (hex, n*v repeats v):
  //   413 93137 10113 10b7 dbc08093 80e7 fe012823 fea10923 fea12423 fe914203 fe4109a3 ff012783 f787b3
  //   f787b3 4b6b7 f0068693 fdc10113 d787b3 10000713 f12423 10593 100793 b00513 2112023 12023 12223 e12623
  //   e12823 f10a23 10b7 a8408093 80e7 2012083 2410113 8067 ff410113 112423 10b7 a7c08093 80e7 513 1800093
  //   80e7 812083 513 c10113 8067 852583 feb12823 fe812e23 3437 a0840413 ff014183 3401b3 1c183 ff114203
  //   440233 24203 4181b3 ff214203 440233 24203 4181b3 ff314203 440233 24203 4181b3 3237 a0020213 320233
  //   24203 ffc12403 420233 420233 410233 11b7 85c18193 fe312823 14800193 fe312623 fec22203 20067 1052703
  //   52683 452783 fe810113 e12423 112a23 fed12823 fef12623 13737 c0070713 fe012223 ff314203 fe4102a3
  //   fef14203 fe410223 fe412203 470233 24203 fe4105a3 ff214203 fe4102a3 fee14203 fe410223 fe412203 470233
  //   24203 fe410523 ff114203 fe4102a3 fed14203 fe410223 fe412203 470233 24203 fe4104a3 ff014203 fe4102a3
  //   fec14203 fe410223 fe412203 470233 24203 fe410423 fe812703 c52603 fee12823 fe812e23 3437 a0840413
  //   ff014183 3401b3 1c183 ff114203 440233 24203 4181b3 ff214203 440233 24203 4181b3 ff314203 440233
  //   24203 4181b3 3237 a0020213 320233 24203 ffc12403 420233 420233 410233 66800193 fe312823 28000193
  //   fe312623 fec22203 20067 c68733 10000513 fe812e23 fe912c23 fee12823 50413 ff012483 fe812423 feb14183
  //   3181b3 fe312423 fe914183 3181b3 fe912423 feb14203 420233 fe412423 fe914203 4181b3 3181b3 fe312a23
  //   fe912423 33237 b0020213 feb14183 4181b3 1c183 fe3103a3 fea14183 4181b3 1c183 fe310323 fe914183
  //   4181b3 1c183 fe3102a3 fe814183 4181b3 1c183 fe310223 ff412183 fe412203 440233 120213 fe412423
  //   feb14203 420233 fe412423 fe914203 4181b3 3237 b0820213 320233 ff812483 ffc12403 24203 420233 420233
  //   410233 11b7 86018193 fe312823 38800193 fe312623 fec22203 20067 812703 10000513 812823 e78733
  //   fe812e23 fe912c23 fee12823 50413 ff012483 fe812423 feb14183 3181b3 fe312423 fe914183 3181b3 fe912423
  //   feb14203 420233 fe412423 fe914203 4181b3 3181b3 fe312a23 fe912423 33237 b0020213 feb14183 4181b3
  //   1c183 fe3103a3 fea14183 4181b3 1c183 fe310323 fe914183 4181b3 1c183 fe3102a3 fe814183 4181b3 1c183
  //   fe310223 ff412183 fe412203 440233 120213 fe412423 feb14203 420233 fe412423 fe914203 4181b3 3237
  //   b0820213 320233 ff812483 ffc12403 24203 420233 420233 410233 11b7 86418193 fe312823 49800193
  //   fe312623 fec22203 20067 8*f787b3 d787b3 f787b3 f787b3 20000437 f40433 812783 c60633 c60633 fef12423
  //   feb14183 3181b3 fe312423 fe914183 fff78213 fe412423 feb14203 420233 fe412423 fe914203 4181b3 3237
  //   b1820213 418233 24203 420233 420233 410233 65800193 fe312823 53c00193 fe312623 fec22203 20067 912623
  //   493 40513 c12223 b12023 10b7 de008093 80e7 12583 412603 812783 148493 40040413 c585b3 fef12823
  //   fe912623 fe812e23 fe912c23 4b437 d0040413 ff014183 340233 100193 320023 fec14183 3401b3 18023 24183
  //   ff114483 940233 100493 920023 fed14483 9404b3 48023 24483 9181b3 ff214483 940233 100493 920023
  //   fee14483 9404b3 48023 24483 9181b3 ff314483 940233 100493 920023 fef14483 9404b3 48023 24483 9181b3
  //   3237 a0020213 320233 24203 ff812483 ffc12403 420233 420233 410233 65400193 fe312823 54400193
  //   fe312623 fec22203 20067 c12483 1012403 1412083 1810113 8067 10000713 fec12823 fee12623 fe812e23
  //   fe912c23 4b437 d0040413 ff014183 340233 100193 320023 fec14183 3401b3 18023 24183 ff114483 940233
  //   100493 920023 fed14483 9404b3 48023 24483 9181b3 ff214483 940233 100493 920023 fee14483 9404b3 48023
  //   24483 9181b3 ff314483 940233 100493 920023 fef14483 9404b3 48023 24483 9181b3 3237 a0020213 320233
  //   24203 ff812483 ffc12403 420233 420233 410233 74c00193 fe312823 28000193 fe312623 fec22203 20067
  //   812703 fee12823 fec12623 fe812e23 fe912c23 4b437 d0040413 ff014183 340233 100193 320023 fec14183
  //   3401b3 18023 24183 ff114483 940233 100493 920023 fed14483 9404b3 48023 24483 9181b3 ff214483 940233
  //   100493 920023 fee14483 9404b3 48023 24483 9181b3 ff314483 940233 100493 920023 fef14483 9404b3 48023
  //   24483 9181b3 3237 a0020213 320233 24203 ff812483 ffc12403 420233 420233 410233 11b7 83418193
  //   fe312823 38800193 fe312623 fec22203 20067 1412083 40637 20000537 1810113 1237 de020213 20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
endmodule

module PC (
  input  [31:0] PC_in,
  input  PC_select,
  input  EN,
  input  clk,
  input  rst,
  output [31:0] PC_out,
  output [31:0] PC_next_out
);

  wire [1:0] register_1_q;
  wire [31:0] multiplexer_1_out;

  Register #(.width(32)) register_1 (
    .D(multiplexer_1_out), .en(EN), .clk(clk), .Q({PC_out[29:0], register_1_q}), .clr(rst));
  Multiplexer #(.width(32)) multiplexer_1 (.in0(PC_next_out), .in1(PC_in), .out(multiplexer_1_out), .sel(PC_select));
  Adder #(.width(32)) adder_1 (.a({PC_out[29:0], register_1_q}), .b(32'h4), .out(PC_next_out));  // open: cin, cout

  assign PC_out[31:30] = 2'b00;

  // Notes on the sheet:
  //   add, addi, lui, lw, lbu, sw, sb, jalr
endmodule

module Fetch (
);
endmodule

module Controller (
  input  [6:0] opcode,
  input  [2:0] funct3,
  input  [6:0] funct7,
  output [1:0] ALUSelect,
  output pcSelect,
  output [2:0] instType,
  output wDSelect,
  output wREN,
  output wMEN,
  output rMEN,
  output wordLS
);

  wire comparator_1_eq, comparator_2_eq, comparator_3_eq, comparator_5_eq, comparator_6_eq, comparator_7_eq,
       comparator_8_eq, comparator_9_eq, nand_1_out, not_1_out, not_2_out, or_1_out, or_2_out, or_3_out,
       or_4_out;

  Comparator #(.width(5)) comparator_1 (.a(opcode[6:2]), .b(5'b01100), .eq(comparator_1_eq));  // open: gt, lt
  Comparator #(.width(5)) comparator_2 (.a(opcode[6:2]), .b(5'b00100), .eq(comparator_2_eq));  // open: gt, lt
  Comparator #(.width(5)) comparator_3 (.a(opcode[6:2]), .b({5{1'b0}}), .eq(comparator_3_eq));  // open: gt, lt
  Comparator #(.width(5)) comparator_4 (.a(opcode[6:2]), .b(5'b11001), .eq(wDSelect));  // open: gt, lt
  Comparator #(.width(5)) comparator_5 (.a(opcode[6:2]), .b(5'b01000), .eq(comparator_5_eq));  // open: gt, lt
  Comparator #(.width(5)) comparator_6 (.a(opcode[6:2]), .b(5'b11000), .eq(comparator_6_eq));  // open: gt, lt
  Comparator #(.width(5)) comparator_7 (.a(opcode[6:2]), .b(5'b01101), .eq(comparator_7_eq));  // open: gt, lt
  Comparator #(.width(5)) comparator_8 (.a(opcode[6:2]), .b(5'b00101), .eq(comparator_8_eq));  // open: gt, lt
  Comparator #(.width(5)) comparator_9 (.a(opcode[6:2]), .b(5'b11101), .eq(comparator_9_eq));  // open: gt, lt
  nand nand_1 (nand_1_out, opcode[0], opcode[1]);
  or or_1 (or_1_out, wDSelect, comparator_9_eq);
  or or_2 (or_2_out, comparator_2_eq, comparator_3_eq, wDSelect);
  or or_3 (or_3_out, comparator_7_eq, comparator_8_eq);
  not not_1 (not_1_out, nand_1_out);
  not not_2 (not_2_out, nand_1_out);
  Comparator #(.width(3)) comparator_10 (.a(funct3), .b(3'b010), .eq(wordLS));  // open: gt, lt
  Priority_Encoder #(.select(2)) priority_encoder_1 (
    .in0(1'b1), .in1(comparator_1_eq), .in2(or_3_out), .out(ALUSelect));  // open: in3, gs, en_out, en_in
  and and_1 (pcSelect, or_1_out, not_1_out);
  Priority_Encoder priority_encoder_2 (
    .in0(comparator_1_eq), .in1(or_2_out), .in2(comparator_5_eq), .in3(comparator_6_eq), .in4(or_3_out),
    .in5(comparator_9_eq), .in6(nand_1_out), .out(instType));  // open: in7, en_in, gs, en_out
  or or_4 (or_4_out, comparator_1_eq, or_2_out, comparator_6_eq, or_3_out, comparator_9_eq);
  and and_2 (wREN, or_4_out, not_2_out);
  and and_3 (wMEN, comparator_5_eq, not_2_out);
  and and_4 (rMEN, comparator_3_eq, not_2_out);
endmodule

module Registers (
  input  clk,
  input  rst,
  input  [3:0] rdR,
  input  [31:0] rdD,
  input  wEN,
  input  [3:0] rs1R,
  input  [3:0] rs2R,
  output [31:0] rs1D,
  output [31:0] rs2D
);

  wire and_1_out, and_2_out, and_3_out, and_4_out, and_5_out, and_6_out, and_7_out, and_8_out, and_9_out,
       and_10_out, and_11_out, and_12_out, and_13_out, and_14_out, and_15_out, decoder_1_out0,
       decoder_1_out1, decoder_1_out2, decoder_1_out3, decoder_2_out0, decoder_2_out1, decoder_2_out2,
       decoder_2_out3;
  wire [31:0] multiplexer_1_out, multiplexer_2_out, multiplexer_3_out, multiplexer_4_out, multiplexer_5_out,
       multiplexer_6_out, multiplexer_7_out, multiplexer_8_out, R1_q, R2_q, R3_q, R4_q, R5_q, R6_q, R7_q,
       R8_q, R9_q, R10_q, R11_q, R12_q, R13_q, R14_q, R15_q;

  Decoder #(.select(2)) decoder_1 (
    .out0(decoder_1_out0), .out1(decoder_1_out1), .out2(decoder_1_out2), .out3(decoder_1_out3),
    .sel(rdR[3:2]), .en(wEN));
  Decoder #(.select(2)) decoder_2 (
    .out0(decoder_2_out0), .out1(decoder_2_out1), .out2(decoder_2_out2), .out3(decoder_2_out3),
    .sel(rdR[1:0]), .en(wEN));
  and and_1 (and_1_out, decoder_2_out1, decoder_1_out0);
  and and_2 (and_2_out, decoder_2_out2, decoder_1_out0);
  and and_3 (and_3_out, decoder_2_out3, decoder_1_out0);
  Register #(.width(32)) R1 (.D(rdD), .en(and_1_out), .clk(clk), .Q(R1_q), .clr(rst));
  Register #(.width(32)) R2 (.D(rdD), .en(and_2_out), .clk(clk), .Q(R2_q), .clr(rst));
  Register #(.width(32)) R3 (.D(rdD), .en(and_3_out), .clk(clk), .Q(R3_q), .clr(rst));
  Register #(.width(32)) R4 (.D(rdD), .en(and_4_out), .clk(clk), .Q(R4_q), .clr(rst));
  and and_4 (and_4_out, decoder_2_out0, decoder_1_out1);
  Register #(.width(32)) R5 (.D(rdD), .en(and_5_out), .clk(clk), .Q(R5_q), .clr(rst));
  and and_5 (and_5_out, decoder_2_out1, decoder_1_out1);
  Register #(.width(32)) R6 (.D(rdD), .en(and_6_out), .clk(clk), .Q(R6_q), .clr(rst));
  and and_6 (and_6_out, decoder_2_out2, decoder_1_out1);
  Register #(.width(32)) R7 (.D(rdD), .en(and_7_out), .clk(clk), .Q(R7_q), .clr(rst));
  and and_7 (and_7_out, decoder_2_out3, decoder_1_out1);
  Register #(.width(32)) R8 (.D(rdD), .en(and_8_out), .clk(clk), .Q(R8_q), .clr(rst));
  and and_8 (and_8_out, decoder_2_out0, decoder_1_out2);
  Register #(.width(32)) R9 (.D(rdD), .en(and_9_out), .clk(clk), .Q(R9_q), .clr(rst));
  and and_9 (and_9_out, decoder_2_out1, decoder_1_out2);
  Register #(.width(32)) R10 (.D(rdD), .en(and_10_out), .clk(clk), .Q(R10_q), .clr(rst));
  and and_10 (and_10_out, decoder_2_out2, decoder_1_out2);
  Register #(.width(32)) R11 (.D(rdD), .en(and_11_out), .clk(clk), .Q(R11_q), .clr(rst));
  and and_11 (and_11_out, decoder_2_out3, decoder_1_out2);
  and and_12 (and_12_out, decoder_2_out0, decoder_1_out3);
  and and_13 (and_13_out, decoder_2_out1, decoder_1_out3);
  and and_14 (and_14_out, decoder_2_out2, decoder_1_out3);
  and and_15 (and_15_out, decoder_2_out3, decoder_1_out3);
  Register #(.width(32)) R12 (.D(rdD), .en(and_12_out), .clk(clk), .Q(R12_q), .clr(rst));
  Register #(.width(32)) R13 (.D(rdD), .en(and_13_out), .clk(clk), .Q(R13_q), .clr(rst));
  Register #(.width(32)) R14 (.D(rdD), .en(and_14_out), .clk(clk), .Q(R14_q), .clr(rst));
  Register #(.width(32)) R15 (.D(rdD), .en(and_15_out), .clk(clk), .Q(R15_q), .clr(rst));
  Multiplexer #(.select(2), .width(32)) multiplexer_1 (
    .in0({32{1'b0}}), .in1(R4_q), .in2(R8_q), .in3(R12_q), .out(multiplexer_1_out), .sel(rs1R[3:2]));
  Multiplexer #(.select(2), .width(32)) multiplexer_2 (
    .in0({32{1'b0}}), .in1(R4_q), .in2(R8_q), .in3(R12_q), .out(multiplexer_2_out), .sel(rs2R[3:2]));
  Multiplexer #(.select(2), .width(32)) multiplexer_3 (
    .in0(R1_q), .in1(R5_q), .in2(R9_q), .in3(R13_q), .out(multiplexer_3_out), .sel(rs1R[3:2]));
  Multiplexer #(.select(2), .width(32)) multiplexer_4 (
    .in0(R1_q), .in1(R5_q), .in2(R9_q), .in3(R13_q), .out(multiplexer_4_out), .sel(rs2R[3:2]));
  Multiplexer #(.select(2), .width(32)) multiplexer_5 (
    .in0(R2_q), .in1(R6_q), .in2(R10_q), .in3(R14_q), .out(multiplexer_5_out), .sel(rs1R[3:2]));
  Multiplexer #(.select(2), .width(32)) multiplexer_6 (
    .in0(R2_q), .in1(R6_q), .in2(R10_q), .in3(R14_q), .out(multiplexer_6_out), .sel(rs2R[3:2]));
  Multiplexer #(.select(2), .width(32)) multiplexer_7 (
    .in0(R3_q), .in1(R7_q), .in2(R11_q), .in3(R15_q), .out(multiplexer_7_out), .sel(rs1R[3:2]));
  Multiplexer #(.select(2), .width(32)) multiplexer_8 (
    .in0(R3_q), .in1(R7_q), .in2(R11_q), .in3(R15_q), .out(multiplexer_8_out), .sel(rs2R[3:2]));
  Multiplexer #(.select(2), .width(32)) multiplexer_9 (
    .in0(multiplexer_1_out), .in1(multiplexer_3_out), .in2(multiplexer_5_out), .in3(multiplexer_7_out),
    .out(rs1D), .sel(rs1R[1:0]));
  Multiplexer #(.select(2), .width(32)) multiplexer_10 (
    .in0(multiplexer_2_out), .in1(multiplexer_4_out), .in2(multiplexer_6_out), .in3(multiplexer_8_out),
    .out(rs2D), .sel(rs2R[1:0]));

  // Notes on the sheet:
  //   R0
endmodule

module Immediate (
  input  [2:0] instType,
  input  [31:0] instruction,
  output [31:0] imm
);

  wire [11:0] bit_extender_4_out;
  wire [19:0] bit_extender_3_out;
  wire [20:0] bit_extender_1_out, bit_extender_2_out;

  assign bit_extender_1_out = {{20{instruction[31]}}, instruction[31]};  // Bit_Extender bit_extender_1
  assign bit_extender_2_out = {{20{instruction[31]}}, instruction[31]};  // Bit_Extender bit_extender_2
  assign bit_extender_3_out = {{19{instruction[31]}}, instruction[31]};  // Bit_Extender bit_extender_3
  assign bit_extender_4_out = {{11{instruction[31]}}, instruction[31]};  // Bit_Extender bit_extender_4
  Multiplexer #(.select(3), .width(32)) multiplexer_1 (
    .in1({bit_extender_1_out, instruction[30:20]}),
    .in2({bit_extender_2_out, instruction[30:25], instruction[11:7]}),
    .in3({bit_extender_3_out, instruction[7], instruction[30:25], instruction[11:8], 1'b0}),
    .in4({instruction[31:12], {12{1'b0}}}),
    .in5({bit_extender_4_out, instruction[19:12], instruction[20], instruction[30:21], 1'b0}), .out(imm),
    .sel(instType));  // open: in0, in6, in7

  // Notes on the sheet:
  //   I_type
  //   S_type
  //   B_type
  //   U_type
  //   J_type
endmodule

module ALU (
  input  [1:0] ALUSelect,
  input  [31:0] A,
  input  [31:0] imm,
  input  [31:0] B,
  output [31:0] C
);

  wire [31:0] multiplexer_1_out, multiplexer_2_out;

  Multiplexer #(.width(32)) multiplexer_1 (.in0(A), .in1({32{1'b0}}), .out(multiplexer_1_out), .sel(ALUSelect[1]));
  Adder #(.width(32)) adder_1 (.a(multiplexer_1_out), .b(multiplexer_2_out), .out(C));  // open: cin, cout
  Multiplexer #(.width(32)) multiplexer_2 (.in0(imm), .in1(B), .out(multiplexer_2_out), .sel(ALUSelect[0]));
endmodule

module Memory (
  input  wordLS,
  input  [31:0] adress,
  input  adressValid,
  input  [31:0] dataIn,
  input  [31:0] readIn,
  output byte3EN,
  output byte2EN,
  output byte1EN,
  output byte0EN,
  output [31:0] adressWord,
  output [31:0] writeOut,
  output [31:0] dataOut
);

  wire decoder_1_out0, decoder_1_out1, decoder_1_out2, decoder_1_out3;
  wire [4:0] shifter_1_out;
  wire [4:2] undriven;
  wire [7:0] multiplexer_1_out;
  wire [31:0] bit_extender_1_out, bit_extender_2_out, bit_extender_3_out, shifter_2_out;

  assign bit_extender_1_out = {{24{1'b0}}, dataIn[7:0]};  // Bit_Extender bit_extender_1
  Shifter #(.width(5)) shifter_1 (.in({undriven, adress[1:0]}), .\dist (3'b011), .out(shifter_1_out));
  Multiplexer #(.select(2), .width(8)) multiplexer_1 (
    .in0(readIn[7:0]), .in1(readIn[15:8]), .in2(readIn[23:16]), .in3(readIn[31:24]), .out(multiplexer_1_out),
    .sel(adress[1:0]));
  assign bit_extender_2_out = {{2{1'b0}}, adress[31:2]};  // Bit_Extender bit_extender_2
  Shifter #(.width(32)) shifter_2 (.in(bit_extender_1_out), .\dist (shifter_1_out), .out(shifter_2_out));
  assign bit_extender_3_out = {{24{1'b0}}, multiplexer_1_out};  // Bit_Extender bit_extender_3
  Decoder #(.select(2)) decoder_1 (
    .out0(decoder_1_out0), .out1(decoder_1_out1), .out2(decoder_1_out2), .out3(decoder_1_out3),
    .sel(adress[1:0]), .en(adressValid));
  Multiplexer #(.width(32)) multiplexer_2 (
    .in0({32{1'b0}}), .in1(bit_extender_2_out), .out(adressWord), .sel(adressValid));
  Multiplexer #(.width(32)) multiplexer_3 (.in0(shifter_2_out), .in1(dataIn), .out(writeOut), .sel(wordLS));
  Multiplexer #(.width(32)) multiplexer_4 (.in0(bit_extender_3_out), .in1(readIn), .out(dataOut), .sel(wordLS));
  or or_1 (byte3EN, wordLS, decoder_1_out3);
  or or_2 (byte2EN, wordLS, decoder_1_out2);
  or or_3 (byte1EN, wordLS, decoder_1_out1);
  or or_4 (byte0EN, wordLS, decoder_1_out0);
endmodule
