// Logisim project F3.circ as structural Verilog: 4 circuits, main circuit main
module main (
  input  \或门 ,
  input  in_2,
  input  \异或门 ,
  input  in_4,
  input  \同或门 ,
  input  in_6,
  input  \_2_4译码器 ,
  input  in_8,
  input  in_9,
  input  in_10,
  input  in_11,
  input  in_12,
  input  in_13,
  input  in_14,
  input  in_15,
  input  in_16,
  input  in_17,
  input  in_18,
  input  in_19,
  input  in_20,
  input  in_21,
  input  in_22,
  input  in_23,
  input  in_24,
  input  in_25,
  input  in_26,
  input  in_27,
  input  in_28,
  input  in_29,
  input  in_30,
  input  in_31,
  input  in_32,
  input  in_33,
  output out_34,
  output out_35,
  output out_36,
  output out_37,
  output out_38,
  output out_39,
  output out_40,
  output out_41
);

  wire and_1_out, and_2_out, and_3_out, and_4_out, and_5_out, and_6_out, decoder2to4_1_out1,
       decoder2to4_1_out2, decoder2to4_1_out3, decoder2to4_1_out4, decoder2to4_2_out1, decoder2to4_2_out2,
       decoder2to4_2_out3, decoder2to4_2_out4, encoder16to4_1_out0, encoder16to4_1_out1, encoder16to4_1_out2,
       encoder16to4_1_out3, nor_1_out, nor_2_out, nor_3_out, not_1_out, not_2_out, not_3_out,
       number7decoder_1_a, number7decoder_1_b, number7decoder_1_c, number7decoder_1_d, number7decoder_1_e,
       number7decoder_1_f, number7decoder_1_g, number7decoder_1_h, number7decoder_2_a, number7decoder_2_b,
       number7decoder_2_c, number7decoder_2_d, number7decoder_2_e, number7decoder_2_f, number7decoder_2_g,
       number7decoder_2_h, or_1_out, transistor_1_out, transistor_2_out, transistor_5_out;

  not not_1 (not_1_out, \_2_4译码器 );
  Transistor #(.\type ("n")) transistor_1 (.in(1'b0), .out(transistor_1_out), .gate(\或门 ));
  and and_1 (and_1_out, \异或门 , in_4);
  and and_2 (and_2_out, \同或门 , in_6);
  not not_2 (not_2_out, in_8);
  and and_3 (and_3_out, \_2_4译码器 , in_8);
  // Probe on and_3_out
  not not_3 (not_3_out, in_11);
  Transistor transistor_2 (.in(1'b1), .out(transistor_2_out), .gate(\或门 ));
  Transistor transistor_3 (.in(transistor_2_out), .out(transistor_1_out), .gate(in_2));
  Transistor #(.\type ("n")) transistor_4 (.in(1'b0), .out(transistor_1_out), .gate(in_2));
  nor nor_1 (nor_1_out, \异或门 , in_4);
  nor nor_2 (nor_2_out, \同或门 , in_6);
  and and_4 (and_4_out, \_2_4译码器 , not_2_out);
  // Probe on and_4_out
  Transistor transistor_5 (.in(1'b1), .out(transistor_5_out), .gate(transistor_1_out));
  LED led_1 (.in(transistor_5_out));
  Transistor #(.\type ("n")) transistor_6 (.in(1'b0), .out(transistor_5_out), .gate(transistor_1_out));
  nor nor_3 (nor_3_out, and_1_out, nor_1_out);
  LED led_2 (.in(nor_3_out));
  or or_1 (or_1_out, and_2_out, nor_2_out);
  LED led_3 (.in(or_1_out));
  and and_5 (and_5_out, not_1_out, in_8);
  // Probe on and_5_out
  // Probe on and_6_out
  and and_6 (and_6_out, not_1_out, not_2_out);
  number7decoder number7decoder_1 (
    .num0(in_12), .num1(in_13), .num2(in_14), .num3(in_15), .point(in_16), .A(number7decoder_1_a),
    .B(number7decoder_1_b), .C(number7decoder_1_c), .D(number7decoder_1_d), .E(number7decoder_1_e),
    .F(number7decoder_1_f), .G(number7decoder_1_g), .H(number7decoder_1_h));
  encoder16to4 encoder16to4_1 (
    .n0(in_17), .n1(in_18), .n2(in_19), .n3(in_20), .n4(in_21), .n5(in_23), .n6(in_24), .n7(in_25),
    .n8(in_26), .n9(in_27), .na(in_28), .nb(in_29), .nc(in_30), .nd(in_31), .ne(in_32), .nf(in_33),
    .out0(encoder16to4_1_out0), .out1(encoder16to4_1_out1), .out2(encoder16to4_1_out2),
    .out3(encoder16to4_1_out3));
  decoder2to4 decoder2to4_1 (
    .in0(in_9), .in1(in_10), .out1(decoder2to4_1_out1), .out2(decoder2to4_1_out2), .out3(decoder2to4_1_out3),
    .out4(decoder2to4_1_out4));
  decoder2to4 decoder2to4_2 (
    .in0(in_9), .in1(in_10), .out1(decoder2to4_2_out1), .out2(decoder2to4_2_out2), .out3(decoder2to4_2_out3),
    .out4(decoder2to4_2_out4));
  _7_Segment_Display u_7_segment_display_1 (
    .g(number7decoder_1_g), .f(number7decoder_1_f), .a(number7decoder_1_a), .b(number7decoder_1_b),
    .e(number7decoder_1_e), .d(number7decoder_1_d), .c(number7decoder_1_c), .dp(number7decoder_1_h));
  and and_7 (out_34, not_3_out, decoder2to4_1_out1);
  and and_8 (out_35, not_3_out, decoder2to4_1_out2);
  and and_9 (out_38, decoder2to4_2_out1, in_11);
  and and_10 (out_39, decoder2to4_2_out2, in_11);
  and and_11 (out_40, decoder2to4_2_out3, in_11);
  and and_12 (out_36, not_3_out, decoder2to4_1_out3);
  and and_13 (out_37, not_3_out, decoder2to4_1_out4);
  and and_14 (out_41, decoder2to4_2_out4, in_11);
  number7decoder number7decoder_2 (
    .num0(encoder16to4_1_out0), .num1(encoder16to4_1_out1), .num2(encoder16to4_1_out2),
    .num3(encoder16to4_1_out3), .point(in_22), .A(number7decoder_2_a), .B(number7decoder_2_b),
    .C(number7decoder_2_c), .D(number7decoder_2_d), .E(number7decoder_2_e), .F(number7decoder_2_f),
    .G(number7decoder_2_g), .H(number7decoder_2_h));
  _7_Segment_Display u_7_segment_display_2 (
    .g(number7decoder_2_g), .f(number7decoder_2_f), .a(number7decoder_2_a), .b(number7decoder_2_b),
    .e(number7decoder_2_e), .d(number7decoder_2_d), .c(number7decoder_2_c), .dp(number7decoder_2_h));

  // Notes on the sheet:
  //   3-8译码器
  //   16-4译码器接数码管
  //   7段数码管
endmodule

module decoder2to4 (
  input  in0,
  input  in1,
  output out1,
  output out2,
  output out3,
  output out4
);

  wire not_1_out, not_2_out;

  not not_1 (not_1_out, in1);
  not not_2 (not_2_out, in0);
  and and_1 (out4, in1, in0);
  and and_2 (out3, in1, not_2_out);
  and and_3 (out2, not_1_out, in0);
  and and_4 (out1, not_1_out, not_2_out);
endmodule

module number7decoder (
  input  num0,
  input  num1,
  input  num2,
  input  num3,
  input  point,
  output A,
  output B,
  output C,
  output D,
  output E,
  output F,
  output G,
  output H
);

  wire n0_out, n1_out, n2_out, n3_out, n4_out, n5_out, n6_out, n7_out, n8_out, n9_out, na_out, nb_out,
       nc_out, nd_out, ne_out, nf_out, not_1_out, not_2_out, not_3_out, not_4_out;

  not not_1 (not_1_out, num0);
  not not_2 (not_2_out, num1);
  not not_3 (not_3_out, num2);
  not not_4 (not_4_out, num3);
  and nf (nf_out, num3, num2, num1, num0);
  or or_1 (A, n0_out, n2_out, n3_out, n5_out, n6_out, n7_out, n8_out, n9_out, na_out, nc_out, ne_out, nf_out);
  and ne (ne_out, num3, num2, num1, not_1_out);
  and nd (nd_out, num3, num2, not_2_out, num0);
  and nc (nc_out, num3, num2, not_2_out, not_1_out);
  or or_2 (B, n0_out, n1_out, n2_out, n3_out, n4_out, n7_out, n8_out, n9_out, na_out, nd_out);
  and nb (nb_out, num3, not_3_out, num1, num0);
  and na (na_out, num3, not_3_out, num1, not_1_out);
  and n9 (n9_out, num3, not_3_out, not_2_out, num0);
  or or_3 (C, n0_out, n1_out, n3_out, n4_out, n5_out, n6_out, n7_out, n8_out, n9_out, na_out, nb_out, nd_out);
  and n8 (n8_out, num3, not_3_out, not_2_out, not_1_out);
  or or_4 (D, n0_out, n2_out, n3_out, n5_out, n6_out, n8_out, n9_out, nb_out, nc_out, nd_out, ne_out);
  and n7 (n7_out, not_4_out, num2, num1, num0);
  and n6 (n6_out, not_4_out, num2, num1, not_1_out);
  and n5 (n5_out, not_4_out, num2, not_2_out, num0);
  or or_5 (E, n0_out, n2_out, n6_out, n8_out, na_out, nb_out, nc_out, nd_out, ne_out, nf_out);
  and n4 (n4_out, not_4_out, num2, not_2_out, not_1_out);
  and n3 (n3_out, not_4_out, not_3_out, num1, num0);
  or or_6 (F, n0_out, n4_out, n5_out, n6_out, n8_out, n9_out, na_out, nb_out, nc_out, ne_out, nf_out);
  and n1 (n1_out, not_4_out, not_3_out, not_2_out, num0);
  and n2 (n2_out, not_4_out, not_3_out, num1, not_1_out);
  or or_7 (G, n2_out, n3_out, n4_out, n5_out, n6_out, n8_out, n9_out, na_out, nb_out, nd_out, ne_out, nf_out);
  and n0 (n0_out, not_4_out, not_3_out, not_2_out, not_1_out);

  assign H = point;
endmodule

module encoder16to4 (
  input  n0,
  input  n1,
  input  n2,
  input  n3,
  input  n4,
  input  n5,
  input  n6,
  input  n7,
  input  n8,
  input  n9,
  input  na,
  input  nb,
  input  nc,
  input  nd,
  input  ne,
  input  nf,
  output out0,
  output out1,
  output out2,
  output out3
);

  or or_1 (out3, n8, n9, na, nb, nc, nd, ne, nf);
  or or_2 (out1, n2, n3, n6, n7, na, nb, ne, nf);
  or or_3 (out2, n4, n5, n6, n7, nc, nd, ne, nf);
  or or_4 (out0, n1, n3, n5, n7, n9, nb, nd, nf);
endmodule
